// Logisim project Compute.circ as structural Verilog
module TickCounter (
  input  Clock,
  input  Enable,
  output out_3,
  output out_4,
  output out_5,
  output out_6
);

  wire not_1_out, O1, O2;

  T_Flip_Flop t_ff_1 (.clk(Clock), .T(1'b1), .Q(O1), .reset(not_1_out), .en(Enable));  // open: Qn, preset
  T_Flip_Flop t_ff_2 (.clk(O1), .T(1'b1), .Q(O2), .reset(not_1_out), .en(Enable));  // open: Qn, preset
  not not_1 (not_1_out, Enable);
  Demultiplexer #(.select(2), .disabled(0), .enable("false")) demultiplexer_1 (
    .out0(out_3), .out1(out_4), .out2(out_5), .out3(out_6), .in(Enable), .sel({O2, O1}));

  // Other names for the same wires on the sheet: CK = Clock; EN = Enable
endmodule

module _8BitIncrement (
  input  Clock,
  input  Enable,
  input  [4:0] Set,
  output [4:0] out_4
);

  wire not_1_out, not_2_out, not_3_out, not_4_out, not_5_out, O1, O2, O3, O4, O5;
  wire [4:0] controlled_inverter_1_out;

  assign controlled_inverter_1_out = Clock ? ~Set : 5'bz;  // Controlled_Inverter controlled_inverter_1
  T_Flip_Flop t_ff_1 (
    .clk(Clock), .T(1'b1), .Q(O1), .preset(controlled_inverter_1_out[0]), .reset(not_1_out), .en(Enable));  // open: Qn
  not not_1 (not_1_out, controlled_inverter_1_out[0]);
  T_Flip_Flop t_ff_2 (
    .clk(O1), .T(1'b1), .Q(O2), .preset(controlled_inverter_1_out[1]), .reset(not_2_out), .en(Enable));  // open: Qn
  not not_2 (not_2_out, controlled_inverter_1_out[1]);
  T_Flip_Flop t_ff_3 (
    .clk(O2), .T(1'b1), .Q(O3), .preset(controlled_inverter_1_out[2]), .reset(not_3_out), .en(Enable));  // open: Qn
  not not_3 (not_3_out, controlled_inverter_1_out[2]);
  T_Flip_Flop t_ff_4 (
    .clk(O3), .T(1'b1), .Q(O4), .preset(controlled_inverter_1_out[3]), .reset(not_4_out), .en(Enable));  // open: Qn
  not not_4 (not_4_out, controlled_inverter_1_out[3]);
  T_Flip_Flop t_ff_5 (
    .clk(O4), .T(1'b1), .Q(O5), .preset(controlled_inverter_1_out[4]), .reset(not_5_out), .en(Enable));  // open: Qn
  not not_5 (not_5_out, controlled_inverter_1_out[4]);
  // NOT_Gate not_6 is placed but not wired
  assign out_4 = ~{O5, O4, O3, O2, O1};  // NOT_Gate not_7, 5 bits wide

  // Other names for the same wires on the sheet: CK = Clock; EN = Enable; ST[4:0] = Set
endmodule

module CommandController (
  input  Clock,
  input  Enable,
  input  [4:0] Set_IC,
  output [4:0] Adress,
  output [2:0] OP_Code
);

  wire [4:0] n8bitincrement_1_out_4;
  wire [7:0] controlled_buffer_1_out, rom_1_data;

  _8BitIncrement u_8bitincrement_1 (.Clock(Clock), .Enable(Enable), .out_4(n8bitincrement_1_out_4), .Set(Set_IC));
  ROM #(.addrWidth(5)) rom_1 (.addr(n8bitincrement_1_out_4), .data(rom_1_data), .sel(Enable));
  assign controlled_buffer_1_out = Enable ? rom_1_data : 8'bz;  // Controlled_Buffer controlled_buffer_1
  Register #(.width(5)) register_1 (
    .D(controlled_buffer_1_out[4:0]), .en(Enable), .Q(Adress), .clk(Clock));  // open: clr
  Register #(.width(3)) register_2 (
    .D(controlled_buffer_1_out[7:5]), .en(Enable), .Q(OP_Code), .clk(Clock));  // open: clr

  // Other names for the same wires on the sheet: CLK = Clock; ENB = Enable; SIC[4:0] = Set_IC

  // Notes on the sheet:
  //   contents of rom_1 (hex, n*v repeats v):
  //   aa 0 aa 13*0 ff 0 aa 10
endmodule

module Computer (
  input  Run,
  input  Reset
);

  wire and_1_out, CK, ENRM, O0, O1, O2, O3, O4, O5, O6, O7, T0, T1, T2, T3;
  wire [2:0] commandcontroller_1_op_code;
  wire [4:0] ADR, INRM;

  Clock clock_1 (.out(CK));
  TickCounter tickcounter_1 (.Clock(CK), .Enable(Run), .out_6(T0), .out_5(T1), .out_4(T2), .out_3(T3));
  assign INRM = Reset ? {5{1'b0}} : 5'bz;  // Controlled_Buffer controlled_buffer_1
  assign INRM = O4 ? ADR : 5'bz;  // Controlled_Buffer controlled_buffer_2
  CommandController commandcontroller_1 (
    .Clock(CK), .Set_IC(INRM), .Enable(ENRM), .Adress(ADR), .OP_Code(commandcontroller_1_op_code));
  Op_Code_Processor op_code_processor_1 (
    .Op_Code(commandcontroller_1_op_code), .out_2(O7), .out_3(O6), .out_4(O5), .out_5(O4), .out_6(O3),
    .out_7(O2), .out_8(O1), .out_9(O0));
  Memory_Handler memory_handler_1 (
    .Clear(Reset), .Clock(CK), .Access_Memory(O0), .Store_Memory(O3), .Address(ADR));  // open: Access_Register, Store_Register, out_8
  and and_1 (and_1_out, O4, T1);
  or or_1 (ENRM, and_1_out, T0);

  // Other names for the same wires on the sheet: RN = Run; RS = Reset
endmodule

module Op_Code_Processor (
  input  [2:0] Op_Code,
  output out_2,
  output out_3,
  output out_4,
  output out_5,
  output out_6,
  output out_7,
  output out_8,
  output out_9
);

  and and_1 (out_2, Op_Code[0], Op_Code[1], Op_Code[2]);
  and and_2 (out_3, ~Op_Code[0], Op_Code[1], Op_Code[2]);  // AND_Gate
  and and_3 (out_5, ~Op_Code[0], ~Op_Code[1], Op_Code[2]);  // AND_Gate
  and and_4 (out_4, Op_Code[0], ~Op_Code[1], Op_Code[2]);  // AND_Gate
  and and_5 (out_7, ~Op_Code[0], Op_Code[1], ~Op_Code[2]);  // AND_Gate
  and and_6 (out_6, Op_Code[0], Op_Code[1], ~Op_Code[2]);  // AND_Gate
  and and_7 (out_8, Op_Code[0], ~Op_Code[1], ~Op_Code[2]);  // AND_Gate
  and and_8 (out_9, ~Op_Code[0], ~Op_Code[1], ~Op_Code[2]);  // AND_Gate
endmodule

module Memory_Handler (
  input  Clear,
  input  Clock,
  input  Access_Memory,
  input  Store_Memory,
  input  Access_Register,
  input  Store_Register,
  input  [4:0] Address,
  output [4:0] out_8
);

  wire buffer_2_out, ENLDA, ENMELD, or_1_out;
  wire [4:0] ADRA, ADRM, OUTA, OUTR;

  or or_1 (or_1_out, Store_Memory, ENMELD);
  assign ADRA = Store_Register ? Address : 5'bz;  // Controlled_Buffer controlled_buffer_1
  Register #(.width(5)) register_1 (.D(ADRA), .en(ENLDA), .Q(OUTA), .clk(Clock), .clr(Clear));
  RAM #(.addrWidth(5), .dataWidth(5)) ram_1 (
    .addr(ADRM), .data(OUTR), .sel(or_1_out), .clk(Clock), .ld(ENMELD), .clr(Clear));
  buf buffer_1 (ENMELD, Access_Memory);
  buf buffer_2 (buffer_2_out, Access_Memory);
  or or_2 (ENLDA, Store_Register, buffer_2_out);
  // Probe on OUTR
  assign ADRM = Access_Memory ? Address : 5'bz;  // Controlled_Buffer controlled_buffer_2
  assign ADRA = Access_Memory ? OUTR : 5'bz;  // Controlled_Buffer controlled_buffer_3
  assign out_8 = Access_Register ? OUTA : 5'bz;  // Controlled_Buffer controlled_buffer_4
  assign ADRM = Store_Memory ? Address : 5'bz;  // Controlled_Buffer controlled_buffer_5

  // Other names for the same wires on the sheet: ADR[4:0] = Address; CLCK = Clock; CLER = Clear; MEAC = Access_Memory;
  //   ENMESL = Store_Memory; MEST = Store_Memory; RGAC = Access_Register; RGST = Store_Register
endmodule
