// Logisim project Yuh.circ as structural Verilog: 9 circuits, main circuit main
module main (
  input  Run,
  input  Clear,
  output OUT
);

  wire Clock_out;
  wire [3:0] cpu_1_out, cpu_1_out_2;

  Hex_Digit_Display hex_digit_display_1 (.value(cpu_1_out_2), .dp(Run));
  CPU cpu_1 (.Run(Run), .Reset(Clear), .STOP(OUT), .OUT({cpu_1_out_2, cpu_1_out}), .Clock(Clock_out));
  Clock Clock (.out(Clock_out));
  Hex_Digit_Display hex_digit_display_2 (.value(cpu_1_out), .dp(Run));
endmodule

module MEM (
  input  Clear,
  input  Clock,
  input  Enable,
  input  [13:0] Data,
  output [7:0] Out
);

  wire C0, C1, C2, C3, RR_W;
  wire [7:0] OM, OR, RD;

  Demultiplexer #(.select(2), .disabled(0)) demultiplexer_1 (
    .out0(C0), .out1(C1), .out2(C2), .out3(C3), .in(1'b1), .sel(Data[13:12]), .en(Enable));
  or or_1 (RR_W, C0, C1);
  assign RD = C0 ? Data[7:0] : 8'bz;  // Controlled_Buffer controlled_buffer_1
  assign RD = C1 ? OM : 8'bz;  // Controlled_Buffer controlled_buffer_2
  MEM___RegisterController mem_registercontroller_1 (
    .Clock(Clock), .Clear(Clear), .DataIn(RD), .Read_Write(RR_W), .Enable(Enable), .out_7(OR),
    .Register(Data[11:8]));
  MEM___IndexController mem_indexcontroller_1 (
    .Address(Data[7:0]), .Data(OR), .Out(OM), .Enable(Enable), .Clock(Clock), .Store_Load(C2), .Clear(Clear));
  assign Out = C3 ? OR : 8'bz;  // Controlled_Buffer controlled_buffer_3

  // Other names for the same wires on the sheet: CK = Clock; CR = Clear; AD[7:0] = Data[7:0]; RG[3:0] = Data[11:8];
  //   EN = Enable
endmodule

module MEM___RegisterController (
  input  Clock,
  input  Clear,
  input  [7:0] DataIn,
  input  Read_Write,
  input  Enable,
  input  [3:0] Register,
  output [7:0] out_7
);

  wire R0, R1, R2, R3, R4, R5, R6, R7, R8, R9, R10, R11, R12, R13, R14, R15;
  wire [7:0] controlled_buffer_1_out, controlled_buffer_2_out, controlled_buffer_3_out,
       controlled_buffer_4_out, controlled_buffer_5_out, controlled_buffer_6_out, controlled_buffer_7_out,
       controlled_buffer_8_out, controlled_buffer_17_out, controlled_buffer_20_out, controlled_buffer_21_out,
       controlled_buffer_24_out, controlled_buffer_25_out, controlled_buffer_27_out,
       controlled_buffer_30_out, controlled_buffer_31_out, register_1_q, register_2_q, register_3_q,
       register_4_q, register_5_q, register_6_q, register_7_q, register_8_q, register_9_q, register_10_q,
       register_11_q, register_12_q, register_13_q, register_14_q, register_15_q, register_16_q;

  Demultiplexer #(.select(4)) demultiplexer_1 (
    .out0(R0), .out1(R1), .out2(R2), .out3(R3), .out4(R4), .out5(R5), .out6(R6), .out7(R7), .out8(R8),
    .out9(R9), .out10(R10), .out11(R11), .out12(R12), .out13(R13), .out14(R14), .out15(R15), .in(1'b1),
    .sel(Register), .en(Enable));
  assign controlled_buffer_1_out = R0 ? DataIn : 8'bz;  // Controlled_Buffer controlled_buffer_1
  Register register_1 (.D(controlled_buffer_1_out), .en(Read_Write), .Q(register_1_q), .clk(Clock), .clr(Clear));
  assign controlled_buffer_2_out = R1 ? DataIn : 8'bz;  // Controlled_Buffer controlled_buffer_2
  Register register_2 (.D(controlled_buffer_2_out), .en(Read_Write), .Q(register_2_q), .clk(Clock), .clr(Clear));
  Register register_3 (.D(controlled_buffer_3_out), .en(Read_Write), .Q(register_3_q), .clk(Clock), .clr(Clear));
  assign controlled_buffer_3_out = R2 ? DataIn : 8'bz;  // Controlled_Buffer controlled_buffer_3
  Register register_4 (.D(controlled_buffer_4_out), .en(Read_Write), .Q(register_4_q), .clk(Clock), .clr(Clear));
  assign controlled_buffer_4_out = R3 ? DataIn : 8'bz;  // Controlled_Buffer controlled_buffer_4
  Register register_5 (.D(controlled_buffer_5_out), .en(Read_Write), .Q(register_5_q), .clk(Clock), .clr(Clear));
  assign controlled_buffer_5_out = R4 ? DataIn : 8'bz;  // Controlled_Buffer controlled_buffer_5
  assign controlled_buffer_6_out = R5 ? DataIn : 8'bz;  // Controlled_Buffer controlled_buffer_6
  Register register_6 (.D(controlled_buffer_6_out), .en(Read_Write), .Q(register_6_q), .clk(Clock), .clr(Clear));
  assign controlled_buffer_7_out = R6 ? DataIn : 8'bz;  // Controlled_Buffer controlled_buffer_7
  Register register_7 (.D(controlled_buffer_7_out), .en(Read_Write), .Q(register_7_q), .clk(Clock), .clr(Clear));
  Register register_8 (.D(controlled_buffer_8_out), .en(Read_Write), .Q(register_8_q), .clk(Clock), .clr(Clear));
  assign controlled_buffer_8_out = R7 ? DataIn : 8'bz;  // Controlled_Buffer controlled_buffer_8
  assign out_7 = R0 ? register_1_q : 8'bz;  // Controlled_Buffer controlled_buffer_9
  assign out_7 = R1 ? register_2_q : 8'bz;  // Controlled_Buffer controlled_buffer_10
  assign out_7 = R2 ? register_3_q : 8'bz;  // Controlled_Buffer controlled_buffer_11
  assign out_7 = R3 ? register_4_q : 8'bz;  // Controlled_Buffer controlled_buffer_12
  assign out_7 = R4 ? register_5_q : 8'bz;  // Controlled_Buffer controlled_buffer_13
  assign out_7 = R5 ? register_6_q : 8'bz;  // Controlled_Buffer controlled_buffer_14
  assign out_7 = R6 ? register_7_q : 8'bz;  // Controlled_Buffer controlled_buffer_15
  assign out_7 = R7 ? register_8_q : 8'bz;  // Controlled_Buffer controlled_buffer_16
  Register register_9 (.D(controlled_buffer_17_out), .en(Read_Write), .Q(register_9_q), .clk(Clock), .clr(Clear));
  assign controlled_buffer_17_out = R8 ? DataIn : 8'bz;  // Controlled_Buffer controlled_buffer_17
  assign out_7 = R8 ? register_9_q : 8'bz;  // Controlled_Buffer controlled_buffer_18
  assign out_7 = R9 ? register_10_q : 8'bz;  // Controlled_Buffer controlled_buffer_19
  Register register_10 (.D(controlled_buffer_20_out), .en(Read_Write), .Q(register_10_q), .clk(Clock), .clr(Clear));
  assign controlled_buffer_20_out = R9 ? DataIn : 8'bz;  // Controlled_Buffer controlled_buffer_20
  Register register_11 (.D(controlled_buffer_21_out), .en(Read_Write), .Q(register_11_q), .clk(Clock), .clr(Clear));
  assign controlled_buffer_21_out = R10 ? DataIn : 8'bz;  // Controlled_Buffer controlled_buffer_21
  assign out_7 = R10 ? register_11_q : 8'bz;  // Controlled_Buffer controlled_buffer_22
  assign out_7 = R11 ? register_12_q : 8'bz;  // Controlled_Buffer controlled_buffer_23
  assign controlled_buffer_24_out = R11 ? DataIn : 8'bz;  // Controlled_Buffer controlled_buffer_24
  Register register_12 (.D(controlled_buffer_24_out), .en(Read_Write), .Q(register_12_q), .clk(Clock), .clr(Clear));
  assign controlled_buffer_25_out = R12 ? DataIn : 8'bz;  // Controlled_Buffer controlled_buffer_25
  Register register_13 (.D(controlled_buffer_25_out), .en(Read_Write), .Q(register_13_q), .clk(Clock), .clr(Clear));
  assign out_7 = R12 ? register_13_q : 8'bz;  // Controlled_Buffer controlled_buffer_26
  Register register_14 (.D(controlled_buffer_27_out), .en(Read_Write), .Q(register_14_q), .clk(Clock), .clr(Clear));
  assign controlled_buffer_27_out = R13 ? DataIn : 8'bz;  // Controlled_Buffer controlled_buffer_27
  assign out_7 = R13 ? register_14_q : 8'bz;  // Controlled_Buffer controlled_buffer_28
  Register register_15 (.D(controlled_buffer_30_out), .en(Read_Write), .Q(register_15_q), .clk(Clock), .clr(Clear));
  assign out_7 = R14 ? register_15_q : 8'bz;  // Controlled_Buffer controlled_buffer_29
  assign controlled_buffer_30_out = R14 ? DataIn : 8'bz;  // Controlled_Buffer controlled_buffer_30
  assign controlled_buffer_31_out = R15 ? DataIn : 8'bz;  // Controlled_Buffer controlled_buffer_31
  assign out_7 = R15 ? register_16_q : 8'bz;  // Controlled_Buffer controlled_buffer_32
  Register register_16 (.D(controlled_buffer_31_out), .en(Read_Write), .Q(register_16_q), .clk(Clock), .clr(Clear));

  // Other names for the same wires on the sheet: CK = Clock; CL = Clear; IN[7:0] = DataIn; OT[7:0] = out_7;
  //   RW = Read_Write
endmodule

module MEM___IndexController (
  input  [7:0] Address,
  input  [7:0] Data,
  input  Enable,
  input  Clock,
  input  Clear,
  input  Store_Load,
  output [7:0] Out
);

  wire not_1_out;

  not not_1 (not_1_out, Store_Load);
  RAM #(.bus("separate")) ram_1 (
    .addr(Address), .din(Data), .data(Out), .str(Store_Load), .sel(Enable), .clk(Clock), .ld(not_1_out),
    .clr(Clear));
endmodule

module CPU (
  input  Clock,
  input  Run,
  input  Reset,
  output [7:0] OUT,
  output STOP
);

  wire BR, DB, MT, or_1_out, Send, ST, XX;
  wire [1:0] controlled_buffer_2_out_2, OP;
  wire [7:0] controlled_buffer_1_out, controlled_buffer_2_out, STO;
  wire [11:8] BC, XC;
  wire [13:0] CC, controlled_buffer_4_out, controlled_buffer_5_out;

  assign controlled_buffer_1_out = Reset ? {8{1'b0}} : 8'bz;  // Controlled_Buffer controlled_buffer_1
  assign {controlled_buffer_2_out_2, BC, controlled_buffer_2_out} = BR ? CC : 14'bz;  // Controlled_Buffer controlled_buffer_2
  BCH bch_1 (.Type(controlled_buffer_2_out_2), .Value(STO), .Out(DB), .Enable(BR));
  // Probe on OP
  // Probe on CC
  CPU___CommandController cpu_commandcontroller_1 (
    .Clock(Clock), .Enable(Run), .Set_IC(controlled_buffer_1_out), .Adress(CC), .OP_Code(OP));
  assign controlled_buffer_1_out = DB ? controlled_buffer_2_out : 8'bz;  // Controlled_Buffer controlled_buffer_3
  Decoder #(.select(2)) decoder_1 (.out0(ST), .out1(MT), .out2(BR), .out3(XX), .sel(OP), .en(Run));
  assign controlled_buffer_4_out = XX ? CC : 14'bz;  // Controlled_Buffer controlled_buffer_4
  or or_1 (or_1_out, ST, BR, Send);
  CON con_1 (.Input(controlled_buffer_4_out), .Enable(XX), .Exit(STOP), .Store(Send), .OUT(XC));
  assign controlled_buffer_5_out = BR ? {2'b11, BC, {8{1'b1}}} : 14'bz;  // Controlled_Buffer controlled_buffer_5
  assign controlled_buffer_5_out = ST ? CC : 14'bz;  // Controlled_Buffer controlled_buffer_6
  MEM mem_1 (.Clear(Reset), .Clock(Clock), .Enable(or_1_out), .Data(controlled_buffer_5_out), .Out(STO));
  assign controlled_buffer_5_out = Send ? {2'b11, XC, {8{1'b1}}} : 14'bz;  // Controlled_Buffer controlled_buffer_7
  // Probe on STO
  Register register_1 (.D(STO), .en(Send), .Q(OUT), .clk(Clock), .clr(Reset));

  // Other names for the same wires on the sheet: CK = Clock; CLR = Reset; RN = Run
endmodule

module CPU___CommandController (
  input  Clock,
  input  Enable,
  input  [7:0] Set_IC,
  output [13:0] Adress,
  output [1:0] OP_Code
);

  wire [7:0] cpu_eightbitincrement_1_out_4;
  wire [15:0] controlled_buffer_1_out, rom_1_data;

  CPU___EightBitIncrement cpu_eightbitincrement_1 (
    .Clock(Clock), .Enable(Enable), .Set(Set_IC), .out_4(cpu_eightbitincrement_1_out_4));
  ROM #(.dataWidth(16)) rom_1 (.addr(cpu_eightbitincrement_1_out_4), .data(rom_1_data), .sel(Enable));
  assign controlled_buffer_1_out = Enable ? rom_1_data : 16'bz;  // Controlled_Buffer controlled_buffer_1
  Register #(.width(14)) register_1 (
    .D(controlled_buffer_1_out[13:0]), .en(Enable), .Q(Adress), .clk(Clock));  // open: clr
  Register #(.width(2)) register_2 (
    .D(controlled_buffer_1_out[15:14]), .en(Enable), .Q(OP_Code), .clk(Clock));  // open: clr

  // Other names for the same wires on the sheet: CLK = Clock; ENB = Enable; SIC[7:0] = Set_IC

  // Notes on the sheet:
  //   contents of rom_1 (hex, n*v repeats v):
  //   4ff 8f0 9400 e8ff ffff
endmodule

module CPU___EightBitIncrement (
  input  Clock,
  input  Enable,
  input  [7:0] Set,
  output [7:0] out_4
);

  wire not_1_out, not_2_out, not_3_out, not_4_out, not_5_out, not_6_out, not_7_out, not_8_out, O1, O2, O3,
       O4, O5, O6, O7, O8;
  wire [7:0] controlled_inverter_1_out;

  assign controlled_inverter_1_out = Clock ? ~Set : 8'bz;  // Controlled_Inverter controlled_inverter_1
  T_Flip_Flop t_ff_1 (
    .clk(Clock), .T(1'b1), .Q(O1), .preset(controlled_inverter_1_out[0]), .reset(not_1_out), .en(Enable));  // open: Qn
  not not_1 (not_1_out, controlled_inverter_1_out[0]);
  T_Flip_Flop t_ff_2 (
    .clk(O1), .T(1'b1), .Q(O2), .preset(controlled_inverter_1_out[1]), .reset(not_2_out), .en(Enable));  // open: Qn
  not not_2 (not_2_out, controlled_inverter_1_out[1]);
  T_Flip_Flop t_ff_3 (
    .clk(O2), .T(1'b1), .Q(O3), .preset(controlled_inverter_1_out[2]), .reset(not_3_out), .en(Enable));  // open: Qn
  not not_3 (not_3_out, controlled_inverter_1_out[2]);
  T_Flip_Flop t_ff_4 (
    .clk(O3), .T(1'b1), .Q(O4), .preset(controlled_inverter_1_out[3]), .reset(not_4_out), .en(Enable));  // open: Qn
  not not_4 (not_4_out, controlled_inverter_1_out[3]);
  T_Flip_Flop t_ff_5 (
    .clk(O4), .T(1'b1), .Q(O5), .preset(controlled_inverter_1_out[4]), .reset(not_5_out), .en(Enable));  // open: Qn
  not not_5 (not_5_out, controlled_inverter_1_out[4]);
  T_Flip_Flop t_ff_6 (
    .clk(O5), .T(1'b1), .Q(O6), .preset(controlled_inverter_1_out[5]), .reset(not_6_out), .en(Enable));  // open: Qn
  not not_6 (not_6_out, controlled_inverter_1_out[5]);
  T_Flip_Flop t_ff_7 (
    .clk(O6), .T(1'b1), .Q(O7), .preset(controlled_inverter_1_out[6]), .reset(not_7_out), .en(Enable));  // open: Qn
  not not_7 (not_7_out, controlled_inverter_1_out[6]);
  T_Flip_Flop t_ff_8 (
    .clk(O7), .T(1'b1), .Q(O8), .preset(controlled_inverter_1_out[7]), .reset(not_8_out), .en(Enable));  // open: Qn
  not not_8 (not_8_out, controlled_inverter_1_out[7]);
  assign out_4 = ~{O8, O7, O6, O5, O4, O3, O2, O1};  // NOT_Gate not_9, 8 bits wide

  // Other names for the same wires on the sheet: CK = Clock; EN = Enable; ST[7:0] = Set
endmodule

module BCH (
  input  Enable,
  input  [1:0] Type,
  input  [7:0] Value,
  output Out
);

  wire and_1_out, and_2_out, and_3_out, and_4_out, and_5_out, and_7_out, and_8_out, and_9_out, B0, not_1_out,
       not_2_out, or_1_out;
  wire [7:0] xnor_1_out;

  assign xnor_1_out = ~(Value ^ {8{1'b0}});  // XNOR_Gate xnor_1, 8 bits wide
  and and_1 (and_1_out, xnor_1_out[7], xnor_1_out[6], xnor_1_out[5], xnor_1_out[4], xnor_1_out[3], xnor_1_out[2], xnor_1_out[1], xnor_1_out[0]);
  and and_2 (and_2_out, and_1_out, B0);
  and and_3 (and_3_out, ~Type[1], ~Type[0]);  // AND_Gate
  and and_4 (and_4_out, ~Type[1], Type[0]);  // AND_Gate
  not not_1 (not_1_out, Value[7]);
  and and_5 (and_5_out, not_1_out, and_4_out);
  and and_6 (B0, Type[1], ~Type[0]);  // AND_Gate
  and and_7 (and_7_out, Type[1], Type[0]);
  and and_8 (and_8_out, Value[7], and_7_out);
  and and_9 (and_9_out, and_5_out, ~and_1_out);  // AND_Gate
  or or_1 (or_1_out, and_8_out, and_9_out, and_3_out, and_2_out);
  assign Out = Enable ? or_1_out : 1'bz;  // Controlled_Buffer controlled_buffer_1
  not not_2 (not_2_out, Enable);
  assign Out = not_2_out ? 1'b0 : 1'bz;  // Controlled_Buffer controlled_buffer_2

  // Other names for the same wires on the sheet: EN = Enable
endmodule

module CON (
  input  [13:0] Input,
  input  Enable,
  output [3:0] OUT,
  output Exit,
  output Store
);

  wire and_1_out, and_2_out, not_1_out, not_2_out;

  and and_1 (and_1_out, Input[13], Input[12]);
  assign Exit = Enable ? and_1_out : 1'bz;  // Controlled_Buffer controlled_buffer_1
  not not_1 (not_1_out, Enable);
  assign Exit = not_1_out ? 1'b0 : 1'bz;  // Controlled_Buffer controlled_buffer_2
  and and_2 (and_2_out, Input[13], ~Input[12]);  // AND_Gate
  assign Store = Enable ? and_2_out : 1'bz;  // Controlled_Buffer controlled_buffer_3
  not not_2 (not_2_out, Enable);
  assign Store = not_2_out ? 1'b0 : 1'bz;  // Controlled_Buffer controlled_buffer_4

  assign OUT = Input[11:8];

  // Other names for the same wires on the sheet: EN = Enable
endmodule
